# Fritzing sketch schema (saved by Fritzing 0.9.3b)
circuit board: 8.46667cm x 5.64444cm
breadboards: 1

parts:
  Digispark2 = Digispark
  LED1 = RGB LED - (4 legs) [package="5 mm [THT]"]
  U2 = POT [package=pot_mammoth]
  R1 = Resistor [tolerance=±5% resistance=330 package=THT]
  R2 = Resistor [tolerance=±5% resistance=330 package=THT]
  R3 = Resistor [tolerance=±5% resistance=330 package=THT]
  U3 = SWITCH_SPDT [package=kps-1290]

nets (from the breadboard view):
  N1: Digispark2.VCC, LED1.common_anode, U2.S
  N2: Digispark2.GND, U2.E
  N3: Digispark2.P0, R1.Pin_1
  N4: Digispark2.P1, R2.Pin_1
  N5: Digispark2.P2, U2.A
  N6: Digispark2.P3, U3.P
  N7: LED1.red_cathode, R1.Pin_0
  N8: LED1.green_cathode, R2.Pin_0
  N9: LED1.blue_cathode, R3.Pin_0
  N10: R3.Pin_1, U3.O

custom parts:
  Digispark: The Digispark is an Attiny85 based microcontroller development board similar to the Arduino line, only cheaper, smaller, and a bit less powerful. With a whole host of shields to extend its functionality and the ability to use the familiar Arduino IDE the Digispark is a great way to jump into electronics, or perfect for when an Arduino is too big or too much.
