# Fritzing sketch schema (saved by Fritzing 0.9.3b)
breadboards: 1

parts:
  Digispark2 = Digispark
  Led = LED - 5mm [color="Red (633nm)" package="5 mm [THT]"]
  R1 = Resistor [tolerance=±5% resistance=220 package="2512 [SMD]"]
  Pulsante = Pushbutton [package="[THT]"]
  Resistenza = Resistor [tolerance=±5% resistance=1k package="2512 [SMD]"]

nets:
  N1: Digispark2.VCC, Resistenza.Pin_1
  N2: Digispark2.GND, Led.anode
  N3: Digispark2.P0, Pulsante.Pin_1, Pulsante.Pin_2
  N4: Digispark2.P1, R1.Pin_1
  N5: Led.cathode, R1.Pin_0
  N6: Pulsante.Pin_3, Pulsante.Pin_4, Resistenza.Pin_0

custom parts:
  Digispark: The Digispark is an Attiny85 based microcontroller development board similar to the Arduino line, only cheaper, smaller, and a bit less powerful. With a whole host of shields to extend its functionality and the ability to use the familiar Arduino IDE the Digispark is a great way to jump into electronics, or perfect for when an Arduino is too big or too much.
