# Fritzing sketch schema_us+bz (saved by Fritzing 0.9.3b)
breadboards: 1

parts:
  Digispark2 = Digispark
  Buzzer = Piezo Speaker
  Sensore_Ultrasuoni = HC-SR04 Ultrasonic Distance Sensor

nets:
  VCC: Digispark2.VCC, Sensore_Ultrasuoni.VCC
  GND: Digispark2.GND, Buzzer.pin1, Sensore_Ultrasuoni.GND
  N1: Digispark2.P0, Buzzer.pin2
  N2: Digispark2.P1, Sensore_Ultrasuoni.TRIG
  N3: Digispark2.P2, Sensore_Ultrasuoni.ECHO

custom parts:
  Digispark: The Digispark is an Attiny85 based microcontroller development board similar to the Arduino line, only cheaper, smaller, and a bit less powerful. With a whole host of shields to extend its functionality and the ability to use the familiar Arduino IDE the Digispark is a great way to jump into electronics, or perfect for when an Arduino is too big or too much.
