# Fritzing sketch schema (saved by Fritzing 0.9.3b)
breadboards: 1

parts:
  Digispark2 = Digispark
  R4 = Resistor [tolerance=±5% resistance=330 package=THT]
  D1 = LTE-302 [package=lte-302]

nets:
  N1: Digispark2.GND, D1.A
  N2: Digispark2.P1, R4.Pin_1
  N3: R4.Pin_0, D1.C

custom parts:
  Digispark: The Digispark is an Attiny85 based microcontroller development board similar to the Arduino line, only cheaper, smaller, and a bit less powerful. With a whole host of shields to extend its functionality and the ability to use the familiar Arduino IDE the Digispark is a great way to jump into electronics, or perfect for when an Arduino is too big or too much.
