# Fritzing sketch schemaLogico (saved by Fritzing 0.9.3b)
circuit board: 8.46667cm x 5.64444cm
breadboards: 1

parts:
  Digispark1 = Digispark
  part = RGB LED - (4 legs) [package="5 mm [THT]"]
  U1 = POT [package=pot_mammoth]

nets:
  N1: Digispark1.VCC, part.common_anode, U1.S
  N2: Digispark1.GND, U1.E
  N3: Digispark1.P0, part.red_cathode
  N4: Digispark1.P1, part.green_cathode
  N5: Digispark1.P2, U1.A
  N6: Digispark1.P3, part.blue_cathode

custom parts:
  Digispark: The Digispark is an Attiny85 based microcontroller development board similar to the Arduino line, only cheaper, smaller, and a bit less powerful. With a whole host of shields to extend its functionality and the ability to use the familiar Arduino IDE the Digispark is a great way to jump into electronics, or perfect for when an Arduino is too big or too much.
